// Logisim project A2.circ as structural Verilog: 1 circuit, main circuit main
module main (
  input  [1:0] Address,
  input  [3:0] Data,
  input  in_3,
  output [3:0] Output
);

  wire _00_out, _01_out, _10_out, _11_out, and_1_out, and_2_out, and_3_out, and_4_out, and_5_out, and_6_out,
       and_7_out, and_8_out, and_9_out, and_10_out, and_11_out, and_12_out, and_13_out, and_14_out,
       and_15_out, and_16_out, and_17_out, and_18_out, and_19_out, and_20_out, and_21_out, and_22_out,
       and_23_out, and_24_out, and_25_out, and_26_out, and_27_out, and_28_out, and_29_out, and_30_out,
       and_31_out, and_32_out, and_33_out, and_34_out, and_35_out, and_36_out, and_37_out, and_38_out,
       and_39_out, and_40_out, and_41_out, and_42_out, and_43_out, and_44_out, and_45_out, and_46_out,
       and_47_out, and_48_out, and_49_out, and_50_out, and_51_out, and_52_out, clock_1_out, d_ff_1_q,
       d_ff_2_q, d_ff_3_q, d_ff_4_q, d_ff_5_q, d_ff_6_q, d_ff_7_q, d_ff_8_q, d_ff_9_q, d_ff_10_q, d_ff_11_q,
       d_ff_12_q, d_ff_13_q, d_ff_14_q, d_ff_15_q, d_ff_16_q, not_1_out, not_2_out, not_3_out, not_4_out,
       not_5_out, or_1_out, or_2_out, or_3_out, or_4_out, or_5_out, or_6_out, or_7_out, or_8_out, or_9_out,
       or_10_out, or_11_out, or_12_out;

  not not_1 (not_1_out, Address[0]);
  and _00 (_00_out, not_1_out, not_2_out);
  not not_2 (not_2_out, Address[1]);
  and _01 (_01_out, Address[0], not_3_out);
  not not_3 (not_3_out, Address[1]);
  not not_4 (not_4_out, Address[0]);
  and _10 (_10_out, not_4_out, Address[1]);
  and _11 (_11_out, Address[0], Address[1]);
  not not_5 (not_5_out, in_3);
  and and_1 (and_1_out, Data[0], _00_out);
  and and_2 (and_2_out, Data[1], _00_out);
  and and_3 (and_3_out, Data[2], _00_out);
  and and_4 (and_4_out, Data[3], _00_out);
  and and_5 (and_5_out, Data[0], _01_out);
  and and_6 (and_6_out, Data[1], _01_out);
  and and_7 (and_7_out, Data[2], _01_out);
  and and_8 (and_8_out, Data[3], _01_out);
  Clock clock_1 (.out(clock_1_out));
  and and_9 (and_9_out, Data[0], _10_out);
  and and_10 (and_10_out, Data[1], _10_out);
  and and_11 (and_11_out, Data[2], _10_out);
  and and_12 (and_12_out, Data[3], _10_out);
  and and_13 (and_13_out, Data[0], _11_out);
  and and_14 (and_14_out, Data[1], _11_out);
  and and_15 (and_15_out, Data[2], _11_out);
  and and_16 (and_16_out, Data[3], _11_out);
  D_Flip_Flop d_ff_1 (.clk(and_17_out), .D(and_1_out), .Q(d_ff_1_q));  // open: Qn, preset, en, reset
  and and_17 (and_17_out, clock_1_out, _00_out, in_3);
  and and_18 (and_18_out, clock_1_out, _00_out, in_3);
  D_Flip_Flop d_ff_2 (.clk(and_18_out), .D(and_2_out), .Q(d_ff_2_q));  // open: Qn, preset, en, reset
  D_Flip_Flop d_ff_3 (.clk(and_19_out), .D(and_3_out), .Q(d_ff_3_q));  // open: Qn, preset, en, reset
  and and_19 (and_19_out, clock_1_out, _00_out, in_3);
  and and_20 (and_20_out, clock_1_out, _00_out, in_3);
  D_Flip_Flop d_ff_4 (.clk(and_20_out), .D(and_4_out), .Q(d_ff_4_q));  // open: Qn, preset, en, reset
  and and_21 (and_21_out, clock_1_out, _01_out, in_3);
  D_Flip_Flop d_ff_5 (.clk(and_21_out), .D(and_5_out), .Q(d_ff_5_q));  // open: Qn, preset, en, reset
  and and_22 (and_22_out, clock_1_out, _01_out, in_3);
  D_Flip_Flop d_ff_6 (.clk(and_22_out), .D(and_6_out), .Q(d_ff_6_q));  // open: Qn, preset, en, reset
  and and_23 (and_23_out, clock_1_out, _01_out, in_3);
  D_Flip_Flop d_ff_7 (.clk(and_23_out), .D(and_7_out), .Q(d_ff_7_q));  // open: Qn, preset, en, reset
  and and_24 (and_24_out, clock_1_out, _01_out, in_3);
  D_Flip_Flop d_ff_8 (.clk(and_24_out), .D(and_8_out), .Q(d_ff_8_q));  // open: Qn, preset, en, reset
  D_Flip_Flop d_ff_9 (.clk(and_25_out), .D(and_9_out), .Q(d_ff_9_q));  // open: Qn, preset, en, reset
  and and_25 (and_25_out, _10_out, clock_1_out, in_3);
  and and_26 (and_26_out, _10_out, clock_1_out, in_3);
  D_Flip_Flop d_ff_10 (.clk(and_26_out), .D(and_10_out), .Q(d_ff_10_q));  // open: Qn, preset, en, reset
  and and_27 (and_27_out, _10_out, in_3, clock_1_out);
  D_Flip_Flop d_ff_11 (.clk(and_27_out), .D(and_11_out), .Q(d_ff_11_q));  // open: Qn, preset, en, reset
  and and_28 (and_28_out, _10_out, clock_1_out, in_3);
  D_Flip_Flop d_ff_12 (.clk(and_28_out), .D(and_12_out), .Q(d_ff_12_q));  // open: Qn, preset, en, reset
  and and_29 (and_29_out, _11_out, clock_1_out, in_3);
  D_Flip_Flop d_ff_13 (.clk(and_29_out), .D(and_13_out), .Q(d_ff_13_q));  // open: Qn, preset, en, reset
  D_Flip_Flop d_ff_14 (.clk(and_30_out), .D(and_14_out), .Q(d_ff_14_q));  // open: Qn, preset, en, reset
  and and_30 (and_30_out, _11_out, in_3, clock_1_out);
  D_Flip_Flop d_ff_15 (.clk(and_31_out), .D(and_15_out), .Q(d_ff_15_q));  // open: Qn, preset, en, reset
  and and_31 (and_31_out, _11_out, in_3, clock_1_out);
  and and_32 (and_32_out, _11_out, in_3, clock_1_out);
  D_Flip_Flop d_ff_16 (.clk(and_32_out), .D(and_16_out), .Q(d_ff_16_q));  // open: Qn, preset, en, reset
  and and_33 (and_33_out, not_5_out, Data[3]);
  and and_34 (and_34_out, _00_out, d_ff_2_q, not_5_out);
  and and_35 (and_35_out, _00_out, d_ff_3_q, not_5_out);
  and and_36 (and_36_out, _00_out, d_ff_4_q, not_5_out);
  and and_37 (and_37_out, _01_out, d_ff_5_q, not_5_out);
  and and_38 (and_38_out, _01_out, d_ff_6_q, not_5_out);
  and and_39 (and_39_out, _01_out, d_ff_7_q, not_5_out);
  and and_40 (and_40_out, _01_out, d_ff_8_q, not_5_out);
  and and_41 (and_41_out, _10_out, d_ff_9_q, not_5_out);
  and and_42 (and_42_out, _10_out, d_ff_10_q, not_5_out);
  and and_43 (and_43_out, _10_out, d_ff_11_q, not_5_out);
  and and_44 (and_44_out, _10_out, d_ff_12_q, not_5_out);
  and and_45 (and_45_out, _11_out, d_ff_13_q, not_5_out);
  and and_46 (and_46_out, _11_out, d_ff_14_q, not_5_out);
  and and_47 (and_47_out, _11_out, d_ff_15_q, not_5_out);
  and and_48 (and_48_out, not_5_out, Data[0]);
  and and_49 (and_49_out, not_5_out, Data[1]);
  and and_50 (and_50_out, not_5_out, Data[2]);
  and and_51 (and_51_out, _00_out, not_5_out, d_ff_1_q);
  and and_52 (and_52_out, _11_out, d_ff_16_q, not_5_out);
  or or_1 (or_1_out, and_41_out, or_4_out);
  or or_2 (or_2_out, and_42_out, or_5_out);
  or or_3 (or_3_out, or_6_out, and_43_out);
  or or_4 (or_4_out, and_45_out, and_48_out);
  or or_5 (or_5_out, and_46_out, and_49_out);
  or or_6 (or_6_out, and_50_out, and_47_out);
  or or_7 (or_7_out, and_33_out, and_52_out);
  or or_8 (or_8_out, and_37_out, or_1_out);
  or or_9 (or_9_out, and_38_out, or_2_out);
  or or_10 (or_10_out, or_3_out, and_39_out);
  or or_11 (or_11_out, or_12_out, and_40_out);
  or or_12 (or_12_out, or_7_out, and_44_out);
  or or_13 (Output[0], and_51_out, or_8_out);
  or or_14 (Output[1], and_34_out, or_9_out);
  or or_15 (Output[2], or_10_out, and_35_out);
  or or_16 (Output[3], or_11_out, and_36_out);

  // Notes on the sheet:
  //   Mode (1=write,0=read)
  //   Clock
  //   DO NOT MOVE the inputs, outputs or clock, Anything else can be moved.
endmodule
