// Logisim project assignment3.circ as structural Verilog: 1 circuit, main circuit main
module main (
  input  in_1,
  input  [3:0] L,
  input  [3:0] R,
  output [3:0] A_OUT,
  output [3:0] out_5
);

  wire and_1_out, and_2_out, and_3_out, and_5_out, and_6_out, and_7_out, and_8_out, and_9_out, and_10_out,
       and_11_out, and_12_out, and_13_out, and_14_out, and_15_out, and_16_out, and_17_out, and_18_out,
       and_19_out, and_20_out, and_21_out, and_22_out, and_23_out, and_24_out, and_25_out, clock_1_out,
       d_ff_1_q, d_ff_2_q, d_ff_3_q, d_ff_4_q, d_ff_5_q, d_ff_7_q, d_ff_9_q, d_ff_13_q, d_ff_16_q, not_1_out,
       not_2_out, not_3_out, not_4_out, not_5_out, not_6_out, not_7_out, not_8_out, or_1_out, or_2_out,
       or_3_out, or_4_out, or_5_out, or_6_out, or_7_out, or_8_out, xor_1_out, xor_2_out, xor_3_out,
       xor_4_out, xor_5_out, xor_6_out, xor_7_out, xor_8_out, xor_9_out, xor_10_out, xor_11_out;

  Clock clock_1 (.out(clock_1_out));
  D_Flip_Flop d_ff_1 (.clk(clock_1_out), .D(L[3]), .Q(d_ff_1_q));  // open: Qn, preset, en, reset
  D_Flip_Flop d_ff_2 (.clk(clock_1_out), .D(L[2]), .Q(d_ff_2_q));  // open: Qn, preset, en, reset
  D_Flip_Flop d_ff_3 (.clk(clock_1_out), .D(L[1]), .Q(d_ff_3_q));  // open: Qn, preset, en, reset
  not not_1 (not_1_out, or_2_out);
  and and_1 (and_1_out, not_1_out, not_2_out);
  D_Flip_Flop d_ff_4 (.clk(clock_1_out), .D(L[0]), .Q(d_ff_4_q));  // open: Qn, preset, en, reset
  not not_2 (not_2_out, d_ff_1_q);
  and and_2 (and_2_out, and_1_out, or_5_out);
  D_Flip_Flop d_ff_5 (.clk(clock_1_out), .D(in_1), .Q(d_ff_5_q));  // open: Qn, preset, en, reset
  not not_3 (not_3_out, d_ff_5_q);
  D_Flip_Flop d_ff_6 (.clk(clock_1_out), .D(xor_3_out), .Q(out_5[3]));  // open: Qn, preset, en, reset
  and and_3 (and_3_out, d_ff_5_q, d_ff_7_q);
  not not_4 (not_4_out, and_3_out);
  xor xor_1 (xor_1_out, not_4_out, and_10_out);
  // AND_Gate and_4 has open pins: in0=not_4_out, in1=and_10_out, out=open
  and and_5 (and_5_out, d_ff_5_q, xor_1_out);
  and and_6 (and_6_out, d_ff_1_q, or_2_out);
  or or_1 (or_1_out, and_6_out, and_8_out);
  D_Flip_Flop d_ff_7 (.clk(clock_1_out), .D(R[3]), .Q(d_ff_7_q));  // open: Qn, preset, en, reset
  and and_7 (and_7_out, d_ff_7_q, not_3_out);
  or or_2 (or_2_out, and_5_out, and_7_out);
  xor xor_2 (xor_2_out, d_ff_1_q, or_2_out);
  xor xor_3 (xor_3_out, xor_2_out, or_5_out);
  and and_8 (and_8_out, xor_2_out, or_5_out);
  or or_3 (or_3_out, xor_3_out, xor_6_out, xor_9_out, xor_11_out);
  not not_5 (not_5_out, or_3_out);
  D_Flip_Flop d_ff_8 (.clk(clock_1_out), .D(and_2_out), .Q(out_5[1]));  // open: Qn, preset, en, reset
  D_Flip_Flop d_ff_9 (.clk(clock_1_out), .D(R[2]), .Q(d_ff_9_q));  // open: Qn, preset, en, reset
  and and_9 (and_9_out, d_ff_5_q, d_ff_9_q);
  not not_6 (not_6_out, and_9_out);
  xor xor_4 (xor_4_out, not_6_out, and_14_out);
  and and_10 (and_10_out, not_6_out, and_14_out);
  and and_11 (and_11_out, d_ff_5_q, xor_4_out);
  or or_4 (or_4_out, and_11_out, and_15_out);
  xor xor_5 (xor_5_out, d_ff_2_q, or_4_out);
  and and_12 (and_12_out, d_ff_2_q, or_4_out);
  and and_13 (and_13_out, xor_5_out, or_7_out);
  or or_5 (or_5_out, and_12_out, and_13_out);
  D_Flip_Flop d_ff_10 (.clk(clock_1_out), .D(xor_3_out), .Q(A_OUT[3]));  // open: Qn, preset, en, reset
  D_Flip_Flop d_ff_11 (.clk(clock_1_out), .D(or_1_out), .Q(out_5[0]));  // open: Qn, preset, en, reset
  and and_14 (and_14_out, not_7_out, and_22_out);
  and and_15 (and_15_out, d_ff_9_q, not_3_out);
  xor xor_6 (xor_6_out, xor_5_out, or_7_out);
  D_Flip_Flop d_ff_12 (.clk(clock_1_out), .D(xor_6_out), .Q(A_OUT[2]));  // open: Qn, preset, en, reset
  D_Flip_Flop d_ff_13 (.clk(clock_1_out), .D(R[1]), .Q(d_ff_13_q));  // open: Qn, preset, en, reset
  and and_16 (and_16_out, d_ff_5_q, d_ff_13_q);
  not not_7 (not_7_out, and_16_out);
  xor xor_7 (xor_7_out, not_7_out, and_22_out);
  and and_17 (and_17_out, d_ff_13_q, not_3_out);
  and and_18 (and_18_out, d_ff_5_q, xor_7_out);
  or or_6 (or_6_out, and_18_out, and_17_out);
  xor xor_8 (xor_8_out, or_6_out, d_ff_3_q);
  and and_19 (and_19_out, or_6_out, d_ff_3_q);
  and and_20 (and_20_out, xor_8_out, and_25_out);
  xor xor_9 (xor_9_out, xor_8_out, and_25_out);
  or or_7 (or_7_out, and_19_out, and_20_out);
  D_Flip_Flop d_ff_14 (.clk(clock_1_out), .D(xor_9_out), .Q(A_OUT[1]));  // open: Qn, preset, en, reset
  D_Flip_Flop d_ff_15 (.clk(clock_1_out), .D(not_5_out), .Q(out_5[2]));  // open: Qn, preset, en, reset
  D_Flip_Flop d_ff_16 (.clk(clock_1_out), .D(R[0]), .Q(d_ff_16_q));  // open: Qn, preset, en, reset
  and and_21 (and_21_out, d_ff_5_q, d_ff_16_q);
  not not_8 (not_8_out, and_21_out);
  xor xor_10 (xor_10_out, not_8_out, d_ff_5_q);
  and and_22 (and_22_out, not_8_out, d_ff_5_q);
  and and_23 (and_23_out, not_3_out, d_ff_16_q);
  and and_24 (and_24_out, d_ff_5_q, xor_10_out);
  or or_8 (or_8_out, and_24_out, and_23_out);
  xor xor_11 (xor_11_out, d_ff_4_q, or_8_out);
  and and_25 (and_25_out, d_ff_4_q, or_8_out);
  D_Flip_Flop d_ff_17 (.clk(clock_1_out), .D(xor_11_out), .Q(A_OUT[0]));  // open: Qn, preset, en, reset

  // Notes on the sheet:
  //   clock
  //   signed overflow
  //   Negative value
  //   Mode( 0 for add, 1 for substract)
  //   overflow
  //   zero value
  //   Status Register
endmodule
